# Fritzing sketch Model (saved by Fritzing 0.9.2b)
breadboards: 1

parts:
  Часть1 = Arduino Uno (Rev3)
  KY-1 = Keyes Relay [package=THT]
  KY-2 = Keyes Relay [package=THT]  # not connected
  KY-3 = Keyes Relay [package=THT]  # not connected
  KY-4 = Keyes Relay [package=THT]  # not connected

nets:
  N1: Часть1.D13/SCK, KY-1.signal
  N2: Часть1.5V, KY-1.power
  N3: Часть1.GND, KY-1.ground

custom parts:
  Keyes Relay: The Keyes 5V relay module is suitable for SCM development, home appliance control. It uses a 5V~12V TIL control signal which can control DC / AC signal.
